# Fritzing sketch fritzing schéma (saved by Fritzing 0.9.2b)
breadboards: 1

parts:
  Composant1 = Arduino Uno (Rev3)
  U3 = POT [package=pot_mammoth]
  S1 = Momentary Switch [package=ksa_sealed_tac_switch]
  LED1 = LEDs [package=led10mm]
  R1 = Resistor [tolerance=±5% resistance=10k package=THT]
  R2 = Resistor [tolerance=±5% resistance=1k package=THT]
  C4 = Electrolytic Capacitor [capacitance=100µF package="300 mil [THT, electrolytic]"]
  U9 = POT [package=pot_mammoth]
  R3 = Resistor [tolerance=±5% resistance=33k package=THT]
  R4 = Resistor [tolerance=±5% resistance=22k package=THT]
  U10 = LM358 [package=dip08]  # not connected
  R1_2 = Resistor [tolerance=±5% resistance=10k package=THT]
  R5 = Trimmer Potentiometer [maximum_resistance=10kΩ package=THT]  # not connected
  R6 = Resistor [tolerance=±5% resistance=1k package=THT]

nets:
  N1: Composant1.A0, R3.Pin_1, R4.Pin_0
  N2: Composant1.A1, U3.S
  N3: Composant1.D2, S1.4
  N4: Composant1.D3_PWM, R2.Pin_0
  N5: Composant1.D4, R6.Pin_0
  N6: Composant1.5V, U3.A
  N7: Composant1.GND, U3.E, S1.1, LED1.C, C4.-, R1_2.Pin_0
  N8: LED1.A, R6.Pin_1
  N9: R1.Pin_0, R1_2.Pin_1
  N10: R2.Pin_1, C4.+
  N11: U9.S, R3.Pin_0
  N12: U9.E, R4.Pin_1

notes:
  pédale
  commande manuelle : manette
  ALIM 5V
  ALIM 12V Véhicule
  Vers consigne pédale du calculateur
  Témoin de mode
  Allumé = manette
  Eteint = pédale
