# Fritzing sketch fritzing schéma (saved by Fritzing 0.9.2b)
breadboards: 1

parts:
  Composant1 = Arduino Uno (Rev3)
  Manuelle = POT [package=pot_mammoth]
  S1 = Momentary Switch [package=ksa_sealed_tac_switch]
  LED1 = LEDs [package=led10mm]  # not connected
  R1 = Resistor [tolerance=±5% resistance=1k package=THT]
  U8 = LM386 [package=dip08]
  R2 = Resistor [tolerance=±5% resistance=1k package=THT]
  R1_2 = Resistor [tolerance=±5% resistance=1k package=THT]
  C4 = Electrolytic Capacitor [capacitance=100µF package="300 mil [THT, electrolytic]"]
  Pédale = POT [package=pot_mammoth]

nets (from the schematic view):
  N1: Composant1.A1, Pédale.A
  N2: Composant1.A5/SCL, Manuelle.A
  N3: Composant1.GND, Manuelle.S, S1.3
  N4: Composant1.D2, S1.2
  N5: Composant1.D3_PWM, R1.Pin_0
  N6: Composant1.5V, Manuelle.E, S1.4, U8.V+
  N7: R1.Pin_1, U8.+IN, C4.+
  N8: U8.-IN, R2.Pin_1, R1_2.Pin_1
  N9: U8.OUT, R2.Pin_0
  N10: R1_2.Pin_0, C4.-

notes:
  pédale
  commande manuelle
